# Fritzing sketch blink_schematics (saved by Fritzing 0.9.3b)
breadboards: 1

parts:
  Raspberry_Pi_1 = Raspberry Pi 3 [part_number=RPI-3-V1.2]
  R2 = Resistor [tolerance=±1% resistance=1k package=THT]
  LED1 = LED - 3mm [color="Red (633nm)" package="3 mm [THT]"]

nets:
  N1: Raspberry_Pi_1.GND, LED1.cathode
  N2: Raspberry_Pi_1.GPIO6, R2.Pin_0
  N3: R2.Pin_1, LED1.anode
